# Fritzing sketch Arduino-Synth (saved by Fritzing 0.8.5b)
breadboards: 1

parts:
  Part1 = Arduino Uno (Rev3)
  R1 = Resistor [tolerance=±5% resistance=470 package=THT]
  C1 = Ceramic Capacitor [capacitance=33nF package="200 mil [THT, multilayer]"]
  C2 = Electrolytic Capacitor [capacitance=1µF voltage=20V package="100 mil [THT, electrolytic]"]
  SPKR1 = Loudspeaker

nets:
  N1: Part1.D3_PWM, R1.Pin_0
  N2: Part1.GND, C1.1, SPKR1.pin1
  N3: R1.Pin_1, C1.0, C2.+
  N4: C2.-, SPKR1.pin2
